// Logisim project jcpu.circ as structural Verilog
module alu (
  input  [7:0] a_in,
  input  [7:0] b_in,
  input  [3:0] op_in,
  output [7:0] data_out
);

  wire [7:0] adder_unit_1_data_out, demultiplexer_1_out0, demultiplexer_1_out1, demultiplexer_2_out0,
       incrementer_unit_1_r_out;

  // Probe on a_in
  // Probe on b_in
  Demultiplexer #(.select(4), .width(8)) demultiplexer_1 (
    .out0(demultiplexer_1_out0), .out1(demultiplexer_1_out1), .in(a_in), .sel(op_in));  // open: out2, out3, out4, out5, out6, out7, out8, out9, out10, out11, out12, out13, out14, out15
  Demultiplexer #(.select(4), .width(8)) demultiplexer_2 (
    .out0(demultiplexer_2_out0), .in(b_in), .sel(op_in));  // open: out1, out2, out3, out4, out5, out6, out7, out8, out9, out10, out11, out12, out13, out14, out15
  adder_unit adder_unit_1 (
    .a_in(demultiplexer_1_out0), .b_in(demultiplexer_2_out0), .data_out(adder_unit_1_data_out));  // open: c_in, c_out
  incrementer_unit incrementer_unit_1 (.a_in(demultiplexer_1_out1), .r_out(incrementer_unit_1_r_out));  // open: c_out
  // Probe on data_out
  Multiplexer #(.select(4), .width(8)) multiplexer_1 (
    .in0(adder_unit_1_data_out), .in1(incrementer_unit_1_r_out), .out(data_out), .sel(op_in));  // open: in2, in3, in4, in5, in6, in7, in8, in9, in10, in11, in12, in13, in14, in15
endmodule

module pc (
  input  [3:0] data_in,
  input  w_in,
  input  s_in,
  input  clk_in,
  output [3:0] data_out
);

  wire controlled_buffer_1_out;
  wire [3:0] incrementer_unit_1_p2, multiplexer_1_out;

  assign controlled_buffer_1_out = w_in ? clk_in : 1'bz;  // Controlled_Buffer controlled_buffer_1
  Multiplexer #(.width(4)) multiplexer_1 (
    .in0(incrementer_unit_1_p2), .in1(data_in), .out(multiplexer_1_out), .sel(s_in));
  D_Flip_Flop d_ff_1 (
    .D(multiplexer_1_out[0]), .clk(controlled_buffer_1_out), .Q(data_out[0]));  // open: Qn, preset, reset
  D_Flip_Flop d_ff_2 (
    .D(multiplexer_1_out[1]), .clk(controlled_buffer_1_out), .Q(data_out[1]));  // open: Qn, preset, reset
  D_Flip_Flop d_ff_3 (
    .D(multiplexer_1_out[2]), .clk(controlled_buffer_1_out), .Q(data_out[2]));  // open: Qn, preset, reset
  D_Flip_Flop d_ff_4 (
    .D(multiplexer_1_out[3]), .clk(controlled_buffer_1_out), .Q(data_out[3]));  // open: Qn, preset, reset
  // incrementer_unit incrementer_unit_1: pin names not known; wires that end beside it: data_out, incrementer_unit_1_p2
endmodule

module adder_unit (
  input  c_in,
  input  [7:0] a_in,
  input  [7:0] b_in,
  output [7:0] data_out,
  output c_out
);

  wire bit_adder_unit_1_c_out, bit_adder_unit_2_c_out, bit_adder_unit_3_c_out, bit_adder_unit_4_c_out,
       bit_adder_unit_5_c_out, bit_adder_unit_6_c_out, bit_adder_unit_7_c_out;

  bit_adder_unit bit_adder_unit_1 (
    .a_in(a_in[0]), .b_in(b_in[0]), .c_in(c_in), .c_out(bit_adder_unit_1_c_out), .r_out(data_out[0]));
  bit_adder_unit bit_adder_unit_2 (
    .a_in(a_in[1]), .b_in(b_in[1]), .c_in(bit_adder_unit_1_c_out), .c_out(bit_adder_unit_2_c_out),
    .r_out(data_out[1]));
  bit_adder_unit bit_adder_unit_3 (
    .a_in(a_in[2]), .b_in(b_in[2]), .c_in(bit_adder_unit_2_c_out), .c_out(bit_adder_unit_3_c_out),
    .r_out(data_out[2]));
  bit_adder_unit bit_adder_unit_4 (
    .a_in(a_in[3]), .b_in(b_in[3]), .c_in(bit_adder_unit_3_c_out), .c_out(bit_adder_unit_4_c_out),
    .r_out(data_out[3]));
  bit_adder_unit bit_adder_unit_5 (
    .a_in(a_in[4]), .b_in(b_in[4]), .c_in(bit_adder_unit_4_c_out), .c_out(bit_adder_unit_5_c_out),
    .r_out(data_out[4]));
  bit_adder_unit bit_adder_unit_6 (
    .a_in(a_in[5]), .b_in(b_in[5]), .c_in(bit_adder_unit_5_c_out), .c_out(bit_adder_unit_6_c_out),
    .r_out(data_out[5]));
  bit_adder_unit bit_adder_unit_7 (
    .a_in(a_in[6]), .b_in(b_in[6]), .c_in(bit_adder_unit_6_c_out), .c_out(bit_adder_unit_7_c_out),
    .r_out(data_out[6]));
  bit_adder_unit bit_adder_unit_8 (
    .a_in(a_in[7]), .b_in(b_in[7]), .c_in(bit_adder_unit_7_c_out), .c_out(c_out), .r_out(data_out[7]));
endmodule

module bit_adder_unit (
  input  c_in,
  input  a_in,
  input  b_in,
  output r_out,
  output c_out
);

  wire and_1_out, and_2_out, xor_1_out;

  xor xor_1 (xor_1_out, a_in, b_in);
  and and_1 (and_1_out, a_in, b_in);
  and and_2 (and_2_out, c_in, xor_1_out);
  xor xor_2 (r_out, c_in, xor_1_out);
  or or_1 (c_out, and_2_out, and_1_out);
endmodule

module subtractor_unit (
  input  op_a_in,
  input  op_b_in,
  input  b_in,
  output s_out,
  output b_out
);

  wire and_1_out, not_1_out, xor_1_out;

  buf xor_1 (xor_1_out, op_a_in);  // XOR_Gate
  buf and_1 (and_1_out, not_1_out);  // AND_Gate
  // NOT_Gate not_1 has open pins: in=open, out=not_1_out
endmodule

module incrementer_unit (
  input  [7:0] a_in,
  output [7:0] r_out,
  output c_out
);

  wire and_1_out, and_2_out, and_3_out, and_4_out, and_5_out, and_6_out, and_7_out;

  xor xor_1 (r_out[0], 1'b1, a_in[0]);
  and and_1 (and_1_out, 1'b1, a_in[0]);
  xor xor_2 (r_out[1], and_1_out, a_in[1]);
  and and_2 (and_2_out, and_1_out, a_in[1]);
  xor xor_3 (r_out[2], and_2_out, a_in[2]);
  and and_3 (and_3_out, and_2_out, a_in[2]);
  xor xor_4 (r_out[3], and_3_out, a_in[3]);
  and and_4 (and_4_out, and_3_out, a_in[3]);
  xor xor_5 (r_out[4], and_4_out, a_in[4]);
  and and_5 (and_5_out, and_4_out, a_in[4]);
  and and_6 (and_6_out, and_5_out, a_in[5]);
  xor xor_6 (r_out[5], and_5_out, a_in[5]);
  xor xor_7 (r_out[6], and_6_out, a_in[6]);
  and and_7 (and_7_out, and_6_out, a_in[6]);
  xor xor_8 (r_out[7], and_7_out, a_in[7]);
  and and_8 (c_out, and_7_out, a_in[7]);
endmodule

module register_unit (
  input  [3:0] data_in,
  input  clk_in,
  output [3:0] data_out
);

  D_Flip_Flop d_ff_1 (.D(data_in[0]), .clk(clk_in));  // open: Q, Qn, preset, reset
  D_Flip_Flop d_ff_2 (.D(data_in[1]), .clk(clk_in));  // open: Q, Qn, preset, reset
  D_Flip_Flop d_ff_3 (.D(data_in[2]), .clk(clk_in));  // open: Q, Qn, preset, reset
  D_Flip_Flop d_ff_4 (.D(data_in[3]), .clk(clk_in));  // open: Q, Qn, preset, reset
endmodule
